// Logisim project Project_rhythm47(Sequential).circ as structural Verilog: 1 circuit, main circuit main
module main (
  input  w,
  input  x,
  input  y,
  output a,
  output b,
  output c,
  output a_2,
  output d,
  output e,
  output f,
  output g,
  output b_2,
  output c_2,
  output a_3,
  output a_4,
  output b_3,
  output b_4,
  output d_2,
  output c_3,
  output c_4,
  output d_3,
  output d_4,
  output e_2,
  output e_3,
  output e_4,
  output f_2,
  output f_3,
  output g_2,
  output f_4,
  output g_3,
  output a_5,
  output g_4,
  output b_5,
  output c_5,
  output d_5,
  output e_5,
  output f_5,
  output g_5,
  output a_6,
  output b_6,
  output c_6,
  output d_6,
  output e_6,
  output a_7,
  output f_6,
  output b_7,
  output g_6,
  output c_7,
  output d_7,
  output e_7,
  output f_7,
  output a_8,
  output g_7,
  output b_8,
  output c_8,
  output d_8,
  output e_8,
  output f_8,
  output g_8
);

  wire and_1_out, and_2_out, and_3_out, and_4_out, and_5_out, and_6_out, and_7_out, and_8_out, and_9_out,
       and_10_out, and_11_out, and_12_out, and_13_out, and_14_out, and_15_out, and_16_out, and_17_out,
       and_18_out, and_19_out, and_20_out, and_21_out, and_22_out, and_23_out, and_24_out, and_25_out,
       and_26_out, and_27_out, and_28_out, and_29_out, and_30_out, and_31_out, and_32_out, and_33_out,
       and_34_out, and_37_out, and_38_out, and_39_out, and_41_out, and_42_out, and_43_out, and_44_out,
       and_51_out, and_52_out, and_53_out, and_54_out, and_55_out, and_56_out, and_63_out, and_64_out,
       and_66_out, and_67_out, and_69_out, and_70_out, and_71_out, and_72_out, and_73_out, and_74_out,
       clock_1_out, clock_2_out, clock_3_out, clock_4_out, clock_5_out, clock_6_out, clock_7_out,
       clock_8_out, clock_9_out, clock_10_out, clock_11_out, j_k_ff_1_q, j_k_ff_2_q, j_k_ff_3_q, j_k_ff_4_q,
       j_k_ff_5_q, j_k_ff_6_q, j_k_ff_7_q, j_k_ff_8_q, j_k_ff_9_q, j_k_ff_10_q, j_k_ff_11_q, j_k_ff_12_q,
       j_k_ff_13_q, j_k_ff_16_q, j_k_ff_17_q, j_k_ff_18_q, j_k_ff_19_q, j_k_ff_20_q, j_k_ff_21_q,
       j_k_ff_22_q, j_k_ff_23_q, j_k_ff_24_q, j_k_ff_25_q, j_k_ff_26_q, j_k_ff_27_q, j_k_ff_28_q,
       j_k_ff_29_q, j_k_ff_30_q, j_k_ff_31_q, j_k_ff_32_q, j_k_ff_33_q, multiplexer_1_out, multiplexer_2_out,
       multiplexer_3_out, multiplexer_4_out, multiplexer_5_out, multiplexer_6_out, multiplexer_7_out,
       n7404_1_pin2, n7404_1_pin4, n7404_1_pin12, n7408_1_pin3, n7408_1_pin11, n7408_2_pin8, n7408_3_pin1,
       n7408_3_pin3, n7408_3_pin6, n7408_3_pin11, n7408_4_pin1, n7408_4_pin3, n7408_4_pin6, n7408_4_pin11,
       n7408_5_pin1, n7408_5_pin3, n7408_5_pin6, n7408_5_pin11, n7408_6_pin3, n7408_7_pin3, n7408_7_pin6,
       n7408_7_pin8, n7408_7_pin11, n7432_1_pin3, n7432_1_pin5, n7432_1_pin8, n7432_1_pin11, n7432_1_pin12,
       n74138_1_pin4, n74138_1_pin6, n74138_1_pin7, n74138_1_pin9, n74138_1_pin10, n74138_1_pin11,
       n74138_1_pin12, n74138_1_pin13, n74138_1_pin14, n74138_1_pin15, nand_1_out, nand_2_out, nand_3_out,
       nand_4_out, nand_5_out, nand_6_out, nand_7_out, nand_8_out, nand_9_out, nand_11_out, nand_12_out,
       nand_13_out, nand_14_out, nand_15_out, nand_16_out, nand_17_out, nand_18_out, nand_19_out,
       nand_20_out, nor_1_out, nor_2_out, nor_3_out, nor_4_out, nor_5_out, nor_6_out, nor_7_out, nor_8_out,
       nor_9_out, nor_10_out, nor_11_out, nor_12_out, nor_13_out, nor_14_out, nor_15_out, nor_16_out,
       nor_17_out, nor_18_out, nor_19_out, nor_20_out, nor_21_out, nor_22_out, nor_24_out, nor_25_out,
       nor_26_out, nor_27_out, nor_29_out, nor_30_out, nor_31_out, nor_32_out, nor_33_out, nor_34_out,
       not_1_out, not_2_out, not_3_out, not_4_out, not_5_out, not_6_out, not_7_out, not_8_out, not_9_out,
       not_10_out, not_11_out, not_12_out, not_13_out, not_14_out, not_15_out, not_16_out, not_17_out,
       not_18_out, not_19_out, or_4_out, or_5_out, or_6_out, or_7_out, or_8_out, or_9_out, or_10_out,
       or_12_out, or_16_out, or_19_out, or_20_out, or_23_out, or_24_out, or_25_out, or_26_out, or_27_out,
       or_28_out, or_29_out, or_30_out, or_31_out, or_32_out, or_33_out, or_34_out, or_35_out, or_36_out,
       or_37_out, or_38_out, or_39_out, or_40_out, or_41_out, or_42_out, or_43_out, or_44_out, or_45_out,
       or_46_out, or_47_out, or_49_out, or_50_out, or_51_out, or_52_out, or_53_out, or_54_out, or_55_out,
       or_56_out, or_57_out, or_58_out, or_59_out, or_60_out, or_61_out, or_63_out, or_64_out, or_65_out,
       or_71_out, or_72_out, or_73_out, or_74_out, or_75_out, or_76_out, or_77_out, xor_1_out, xor_2_out,
       xor_3_out, xor_4_out, xor_5_out, xor_6_out;
  wire [1:0] j_k_ff_14_q;

  Clock clock_1 (.out(clock_1_out));
  J_K_Flip_Flop j_k_ff_1 (.J(1'b1), .K(1'b1), .clk(clock_1_out), .Q(j_k_ff_1_q));  // open: Qn, preset, reset
  J_K_Flip_Flop j_k_ff_2 (
    .J(j_k_ff_1_q), .K(j_k_ff_1_q), .clk(clock_1_out), .Q(j_k_ff_2_q));  // open: Qn, preset, reset
  Clock clock_2 (.out(clock_2_out));
  and and_1 (and_1_out, j_k_ff_1_q, j_k_ff_2_q);
  J_K_Flip_Flop j_k_ff_3 (.J(and_1_out), .K(and_1_out), .clk(clock_1_out), .Q(j_k_ff_3_q));  // open: Qn, preset, reset
  J_K_Flip_Flop j_k_ff_4 (.J(1'b1), .K(1'b1), .clk(clock_3_out), .Q(j_k_ff_4_q));  // open: Qn, preset, reset
  Clock clock_3 (.out(clock_3_out));
  J_K_Flip_Flop j_k_ff_5 (.J(1'b1), .K(1'b1), .clk(clock_2_out), .Q(j_k_ff_5_q));  // open: Qn, preset, reset
  J_K_Flip_Flop j_k_ff_6 (
    .J(j_k_ff_5_q), .K(j_k_ff_5_q), .clk(clock_2_out), .Q(j_k_ff_6_q));  // open: Qn, preset, reset
  J_K_Flip_Flop j_k_ff_7 (
    .J(j_k_ff_4_q), .K(j_k_ff_4_q), .clk(clock_3_out), .Q(j_k_ff_7_q));  // open: Qn, preset, reset
  and and_2 (and_2_out, j_k_ff_5_q, j_k_ff_6_q);
  J_K_Flip_Flop j_k_ff_8 (.J(and_2_out), .K(and_2_out), .clk(clock_2_out), .Q(j_k_ff_8_q));  // open: Qn, preset, reset
  and and_3 (and_3_out, j_k_ff_4_q, j_k_ff_7_q);
  J_K_Flip_Flop j_k_ff_9 (.J(and_3_out), .K(and_3_out), .clk(clock_3_out), .Q(j_k_ff_9_q));  // open: Qn, preset, reset
  _7404 #(.ShowInternalStructure("true")) u_7404_1 (
    .pin1(j_k_ff_1_q), .pin2(n7404_1_pin2), .pin3(j_k_ff_2_q), .pin4(n7404_1_pin4), .pin13(j_k_ff_3_q),
    .pin12(n7404_1_pin12));  // open: pin5, pin6, pin11, pin10, pin9, pin8
  _7408 #(.ShowInternalStructure("true")) u_7408_1 (
    .pin1(j_k_ff_2_q), .pin2(n7404_1_pin2), .pin3(n7408_1_pin3), .pin13(n7404_1_pin12), .pin12(j_k_ff_2_q),
    .pin11(n7408_1_pin11));  // open: pin4, pin5, pin6, pin10, pin9, pin8
  _7432 #(.ShowInternalStructure("true")) u_7432_1 (
    .pin1(n7404_1_pin2), .pin2(j_k_ff_3_q), .pin3(n7432_1_pin3), .pin4(j_k_ff_3_q), .pin5(n7432_1_pin5),
    .pin6(c), .pin13(n7408_1_pin11), .pin12(n7432_1_pin12), .pin11(n7432_1_pin11), .pin10(n7404_1_pin12),
    .pin9(n7404_1_pin2), .pin8(n7432_1_pin8));
  _7408 #(.ShowInternalStructure("true")) u_7408_2 (
    .pin1(j_k_ff_3_q), .pin2(j_k_ff_1_q), .pin3(a), .pin4(n7432_1_pin3), .pin5(j_k_ff_2_q), .pin6(b),
    .pin13(n7404_1_pin12), .pin12(j_k_ff_2_q), .pin11(d), .pin10(n7404_1_pin12), .pin9(j_k_ff_1_q),
    .pin8(n7408_2_pin8));
  _7432 #(.ShowInternalStructure("true")) u_7432_2 (
    .pin1(n7432_1_pin11), .pin2(n7408_1_pin3), .pin3(f), .pin4(n7408_2_pin8), .pin5(n7404_1_pin4), .pin6(e),
    .pin13(n7432_1_pin8), .pin12(n7404_1_pin4), .pin11(g));  // open: pin10, pin9, pin8
  not not_1 (not_1_out, j_k_ff_9_q);
  not not_2 (not_2_out, j_k_ff_7_q);
  _7486 #(.ShowInternalStructure("true")) u_7486_1 (
    .pin1(j_k_ff_2_q), .pin2(j_k_ff_1_q), .pin3(n7432_1_pin5), .pin13(j_k_ff_3_q), .pin12(j_k_ff_1_q),
    .pin11(n7432_1_pin12));  // open: pin4, pin5, pin6, pin10, pin9, pin8
  J_K_Flip_Flop j_k_ff_10 (.J(1'b1), .K(1'b1), .clk(clock_4_out), .Q(j_k_ff_10_q));  // open: Qn, preset, reset
  Clock clock_4 (.out(clock_4_out));
  not not_3 (not_3_out, j_k_ff_4_q);
  and and_4 (and_4_out, j_k_ff_9_q, not_2_out, j_k_ff_4_q);
  and and_5 (and_5_out, j_k_ff_9_q, j_k_ff_7_q, j_k_ff_4_q);
  and and_6 (and_6_out, not_1_out, j_k_ff_7_q, not_3_out);
  and and_7 (and_7_out, not_1_out, not_2_out, j_k_ff_4_q);
  and and_8 (and_8_out, j_k_ff_9_q, not_2_out, j_k_ff_4_q);
  and and_9 (and_9_out, not_1_out, j_k_ff_7_q, not_3_out);
  and and_10 (and_10_out, not_1_out, j_k_ff_7_q, j_k_ff_4_q);
  and and_11 (and_11_out, not_1_out, not_2_out, not_3_out);
  and and_12 (and_12_out, j_k_ff_9_q, not_2_out, not_3_out);
  and and_13 (and_13_out, not_1_out, not_2_out, j_k_ff_4_q);
  and and_14 (and_14_out, not_1_out, j_k_ff_7_q, j_k_ff_4_q);
  and and_15 (and_15_out, j_k_ff_9_q, j_k_ff_7_q, not_3_out);
  and and_16 (and_16_out, not_1_out, not_2_out, not_3_out);
  and and_17 (and_17_out, not_1_out, not_2_out, j_k_ff_4_q);
  and and_18 (and_18_out, not_1_out, j_k_ff_7_q, not_3_out);
  and and_19 (and_19_out, not_1_out, j_k_ff_7_q, j_k_ff_4_q);
  and and_20 (and_20_out, j_k_ff_9_q, not_2_out, not_3_out);
  and and_21 (and_21_out, j_k_ff_9_q, not_2_out, j_k_ff_4_q);
  and and_22 (and_22_out, j_k_ff_9_q, j_k_ff_7_q, not_3_out);
  nor nor_1 (nor_1_out, j_k_ff_8_q, j_k_ff_8_q);
  nor nor_2 (nor_2_out, j_k_ff_5_q, j_k_ff_5_q);
  nor nor_3 (nor_3_out, j_k_ff_8_q, j_k_ff_8_q);
  nor nor_4 (nor_4_out, j_k_ff_6_q, j_k_ff_6_q);
  nor nor_5 (nor_5_out, j_k_ff_8_q, j_k_ff_8_q);
  nor nor_6 (nor_6_out, j_k_ff_6_q, j_k_ff_6_q);
  nor nor_7 (nor_7_out, j_k_ff_5_q, j_k_ff_5_q);
  nor nor_8 (nor_8_out, j_k_ff_6_q, j_k_ff_6_q);
  nor nor_9 (nor_9_out, j_k_ff_6_q, j_k_ff_6_q);
  nor nor_10 (nor_10_out, j_k_ff_5_q, j_k_ff_5_q);
  nor nor_11 (nor_11_out, j_k_ff_5_q, j_k_ff_5_q);
  nor nor_12 (nor_12_out, j_k_ff_6_q, j_k_ff_6_q);
  nor nor_13 (nor_13_out, j_k_ff_8_q, j_k_ff_8_q);
  nor nor_14 (nor_14_out, j_k_ff_6_q, j_k_ff_6_q);
  nor nor_15 (nor_15_out, j_k_ff_8_q, j_k_ff_8_q);
  nor nor_16 (nor_16_out, j_k_ff_6_q, j_k_ff_6_q);
  nor nor_17 (nor_17_out, j_k_ff_5_q, j_k_ff_5_q);
  J_K_Flip_Flop j_k_ff_11 (
    .J(j_k_ff_10_q), .K(j_k_ff_10_q), .clk(clock_4_out), .Q(j_k_ff_11_q));  // open: Qn, preset, reset
  or or_1 (a_5, and_4_out, and_5_out);
  and and_23 (and_23_out, j_k_ff_9_q, j_k_ff_7_q, not_3_out);
  and and_24 (and_24_out, j_k_ff_9_q, j_k_ff_7_q, j_k_ff_4_q);
  and and_25 (and_25_out, not_1_out, j_k_ff_7_q, not_3_out);
  and and_26 (and_26_out, j_k_ff_9_q, j_k_ff_7_q, not_3_out);
  and and_27 (and_27_out, not_1_out, j_k_ff_7_q, j_k_ff_4_q);
  nor nor_18 (nor_18_out, nor_3_out, nor_4_out);
  nor nor_19 (nor_19_out, nor_4_out, j_k_ff_5_q);
  nor nor_20 (nor_20_out, nor_5_out, nor_5_out);
  nor nor_21 (nor_21_out, nor_6_out, j_k_ff_5_q);
  nor nor_22 (nor_22_out, nor_7_out, j_k_ff_6_q);
  nor nor_23 (d_7, j_k_ff_8_q, nor_8_out);
  nor nor_24 (nor_24_out, nor_10_out, j_k_ff_8_q);
  nor nor_25 (nor_25_out, nor_12_out, j_k_ff_8_q);
  nor nor_26 (nor_26_out, nor_13_out, j_k_ff_5_q);
  nor nor_27 (nor_27_out, nor_14_out, j_k_ff_5_q);
  and and_28 (and_28_out, j_k_ff_10_q, j_k_ff_11_q);
  and and_29 (and_29_out, j_k_ff_9_q, j_k_ff_7_q, j_k_ff_4_q);
  or or_2 (d_5, and_9_out, and_10_out);
  and and_30 (and_30_out, not_1_out, not_2_out, j_k_ff_4_q);
  and and_31 (and_31_out, j_k_ff_9_q, not_2_out, j_k_ff_4_q);
  and and_32 (and_32_out, not_1_out, j_k_ff_7_q, not_3_out);
  and and_33 (and_33_out, j_k_ff_9_q, not_2_out, not_3_out);
  nor nor_28 (a_7, nor_1_out, nor_2_out);
  nor nor_29 (nor_29_out, nor_18_out, nor_19_out);
  nor nor_30 (nor_30_out, j_k_ff_8_q, nor_11_out);
  nor nor_31 (nor_31_out, nor_15_out, nor_16_out, nor_17_out);
  J_K_Flip_Flop j_k_ff_12 (
    .J(and_28_out), .K(and_28_out), .clk(clock_4_out), .Q(j_k_ff_12_q));  // open: Qn, preset, reset
  or or_3 (b_5, and_23_out, and_6_out, and_24_out);
  and and_34 (and_34_out, j_k_ff_9_q, not_2_out, not_3_out);
  or or_4 (or_4_out, and_16_out, and_17_out, and_18_out);
  nor nor_32 (nor_32_out, nor_20_out, nor_21_out, nor_22_out);
  nor nor_33 (nor_33_out, nor_9_out, nor_24_out);
  nor nor_34 (nor_34_out, nor_30_out, nor_25_out, nor_26_out, nor_27_out);
  nor nor_35 (g_7, nor_31_out, nor_31_out);
  or or_5 (or_5_out, and_11_out, and_30_out);
  or or_6 (or_6_out, and_27_out, and_12_out, and_31_out);
  or or_7 (or_7_out, and_13_out, and_32_out, and_15_out);
  or or_8 (or_8_out, and_19_out, and_20_out, and_21_out);
  nor nor_36 (b_7, nor_29_out, nor_29_out);
  nor nor_37 (f_7, nor_34_out, nor_34_out);
  or or_9 (or_9_out, and_7_out, and_25_out, and_34_out);
  or or_10 (or_10_out, and_26_out, and_8_out, and_29_out);
  or or_11 (f_5, or_7_out, or_12_out);
  or or_12 (or_12_out, and_14_out, and_33_out);
  or or_13 (g_5, or_4_out, or_8_out, and_22_out);
  nor nor_38 (c_7, nor_32_out, nor_32_out);
  nor nor_39 (e_7, nor_33_out, nor_33_out);
  or or_14 (c_5, or_9_out, or_10_out);
  or or_15 (e_5, or_5_out, or_6_out);
  Clock clock_5 (.out(clock_5_out));
  not not_4 (not_4_out, j_k_ff_10_q);
  not not_5 (not_5_out, j_k_ff_12_q);
  not not_6 (not_6_out, j_k_ff_11_q);
  J_K_Flip_Flop j_k_ff_13 (.J(1'b1), .K(1'b1), .clk(clock_5_out), .Q(j_k_ff_13_q));  // open: Qn, preset, reset
  and and_35 (a_4, j_k_ff_12_q, j_k_ff_10_q);
  or or_16 (or_16_out, not_4_out, j_k_ff_12_q);
  J_K_Flip_Flop j_k_ff_14 (
    .J(j_k_ff_13_q), .K(j_k_ff_13_q), .clk(clock_5_out), .Q(j_k_ff_14_q[0]));  // open: Qn, preset, reset
  xor xor_1 (xor_1_out, j_k_ff_11_q, j_k_ff_10_q);
  and and_36 (d_3, not_5_out, j_k_ff_11_q);
  and and_37 (and_37_out, not_5_out, j_k_ff_10_q);
  and and_38 (and_38_out, not_5_out, j_k_ff_11_q);
  xor xor_2 (xor_2_out, j_k_ff_12_q, j_k_ff_10_q);
  and and_39 (and_39_out, j_k_ff_13_q, j_k_ff_14_q[0]);
  J_K_Flip_Flop j_k_ff_15 (
    .J(and_39_out), .K(and_39_out), .clk(clock_5_out), .Q(j_k_ff_14_q[1]));  // open: Qn, preset, reset
  and and_40 (b_4, or_16_out, j_k_ff_11_q);
  or or_17 (c_3, xor_1_out, j_k_ff_12_q);
  or or_18 (e_2, and_37_out, not_6_out);
  and and_41 (and_41_out, j_k_ff_11_q, not_4_out);
  or or_19 (or_19_out, and_38_out, xor_2_out);
  or or_20 (or_20_out, not_5_out, not_6_out);
  or or_21 (g_2, not_4_out, or_20_out);
  Clock clock_6 (.out(clock_6_out));
  or or_22 (f_2, and_41_out, or_19_out);
  J_K_Flip_Flop j_k_ff_16 (.J(1'b1), .K(1'b1), .clk(clock_6_out), .Q(j_k_ff_16_q));  // open: Qn, preset, reset
  Clock clock_7 (.out(clock_7_out));
  J_K_Flip_Flop j_k_ff_17 (.J(1'b1), .K(1'b1), .clk(clock_8_out), .Q(j_k_ff_17_q));  // open: Qn, preset, reset
  Clock clock_8 (.out(clock_8_out));
  J_K_Flip_Flop j_k_ff_18 (.J(1'b1), .K(1'b1), .clk(clock_7_out), .Q(j_k_ff_18_q));  // open: Qn, preset, reset
  J_K_Flip_Flop j_k_ff_19 (
    .J(j_k_ff_16_q), .K(j_k_ff_16_q), .clk(clock_6_out), .Q(j_k_ff_19_q));  // open: Qn, preset, reset
  J_K_Flip_Flop j_k_ff_20 (
    .J(j_k_ff_18_q), .K(j_k_ff_18_q), .clk(clock_7_out), .Q(j_k_ff_20_q));  // open: Qn, preset, reset
  J_K_Flip_Flop j_k_ff_21 (
    .J(j_k_ff_17_q), .K(j_k_ff_17_q), .clk(clock_8_out), .Q(j_k_ff_21_q));  // open: Qn, preset, reset
  and and_42 (and_42_out, j_k_ff_16_q, j_k_ff_19_q);
  J_K_Flip_Flop j_k_ff_22 (
    .J(and_42_out), .K(and_42_out), .clk(clock_6_out), .Q(j_k_ff_22_q));  // open: Qn, preset, reset
  and and_43 (and_43_out, j_k_ff_18_q, j_k_ff_20_q);
  J_K_Flip_Flop j_k_ff_23 (
    .J(and_43_out), .K(and_43_out), .clk(clock_7_out), .Q(j_k_ff_23_q));  // open: Qn, preset, reset
  and and_44 (and_44_out, j_k_ff_17_q, j_k_ff_21_q);
  J_K_Flip_Flop j_k_ff_24 (
    .J(and_44_out), .K(and_44_out), .clk(clock_8_out), .Q(j_k_ff_24_q));  // open: Qn, preset, reset
  Multiplexer #(.select(2)) multiplexer_1 (
    .in0(1'b0), .in1(1'b0), .in2(j_k_ff_13_q), .in3(j_k_ff_13_q), .out(multiplexer_1_out), .sel(j_k_ff_14_q));
  not not_7 (not_7_out, j_k_ff_13_q);
  Multiplexer #(.select(2)) multiplexer_2 (
    .in0(1'b0), .in1(not_7_out), .in2(1'b0), .in3(1'b1), .out(multiplexer_2_out), .sel(j_k_ff_14_q));
  Multiplexer #(.select(2)) multiplexer_3 (
    .in0(j_k_ff_13_q), .in1(not_7_out), .in2(1'b1), .in3(1'b1), .out(multiplexer_3_out), .sel(j_k_ff_14_q));
  Multiplexer #(.select(2)) multiplexer_4 (
    .in0(1'b0), .in1(1'b1), .in2(1'b0), .in3(1'b0), .out(multiplexer_4_out), .sel(j_k_ff_14_q));
  Multiplexer #(.select(2)) multiplexer_5 (
    .in0(1'b1), .in1(j_k_ff_13_q), .in2(1'b1), .in3(1'b0), .out(multiplexer_5_out), .sel(j_k_ff_14_q));
  Multiplexer #(.select(2)) multiplexer_6 (
    .in0(j_k_ff_13_q), .in1(1'b1), .in2(not_7_out), .in3(not_7_out), .out(multiplexer_6_out),
    .sel(j_k_ff_14_q));
  Multiplexer #(.select(2)) multiplexer_7 (
    .in0(1'b1), .in1(1'b1), .in2(1'b1), .in3(not_7_out), .out(multiplexer_7_out), .sel(j_k_ff_14_q));
  _74138 #(.ShowInternalStructure("true")) u_74138_1 (
    .pin1(j_k_ff_16_q), .pin2(j_k_ff_19_q), .pin3(j_k_ff_22_q), .pin4(n74138_1_pin4), .pin5(n74138_1_pin4),
    .pin6(n74138_1_pin6), .pin7(n74138_1_pin7), .pin15(n74138_1_pin15), .pin14(n74138_1_pin14),
    .pin13(n74138_1_pin13), .pin12(n74138_1_pin12), .pin11(n74138_1_pin11), .pin10(n74138_1_pin10),
    .pin9(n74138_1_pin9));
  _7408 #(.ShowInternalStructure("true")) u_7408_3 (
    .pin1(n7408_3_pin1), .pin2(n74138_1_pin12), .pin3(n7408_3_pin3), .pin4(n7408_3_pin3),
    .pin5(n74138_1_pin11), .pin6(n7408_3_pin6), .pin13(n74138_1_pin15), .pin12(n74138_1_pin14),
    .pin11(n7408_3_pin11), .pin10(n7408_3_pin11), .pin9(n74138_1_pin13), .pin8(n7408_3_pin1));
  _7_Segment_Display u_7_segment_display_1 (
    .g(multiplexer_7_out), .f(multiplexer_6_out), .a(multiplexer_1_out), .b(multiplexer_2_out),
    .e(multiplexer_5_out), .d(multiplexer_4_out), .c(multiplexer_3_out));  // open: dp
  not not_8 (not_8_out, j_k_ff_24_q);
  not not_9 (not_9_out, j_k_ff_21_q);
  not not_10 (not_10_out, j_k_ff_17_q);
  _7408 #(.ShowInternalStructure("true")) u_7408_4 (
    .pin1(n7408_4_pin1), .pin2(n74138_1_pin11), .pin3(n7408_4_pin3), .pin4(n7408_4_pin3),
    .pin5(n74138_1_pin10), .pin6(n7408_4_pin6), .pin13(n7408_3_pin6), .pin12(n74138_1_pin9),
    .pin11(n7408_4_pin11), .pin10(n7408_3_pin11), .pin9(n74138_1_pin12), .pin8(n7408_4_pin1));
  _7_Segment_Display u_7_segment_display_2 (
    .g(n74138_1_pin7), .f(n7408_7_pin8), .a(n7408_4_pin11), .b(n7408_4_pin6), .e(n7408_7_pin6),
    .d(n7408_6_pin3), .c(n7408_5_pin11));  // open: dp
  nand nand_1 (nand_1_out, j_k_ff_23_q, j_k_ff_23_q);
  nand nand_2 (nand_2_out, j_k_ff_23_q, j_k_ff_23_q);
  or or_23 (or_23_out, j_k_ff_24_q, j_k_ff_21_q, j_k_ff_17_q);
  or or_24 (or_24_out, j_k_ff_24_q, j_k_ff_21_q, not_10_out);
  or or_25 (or_25_out, j_k_ff_24_q, not_9_out, j_k_ff_17_q);
  or or_26 (or_26_out, j_k_ff_24_q, not_9_out, not_10_out);
  or or_27 (or_27_out, not_8_out, j_k_ff_21_q, j_k_ff_17_q);
  or or_28 (or_28_out, not_8_out, not_9_out, j_k_ff_17_q);
  or or_29 (or_29_out, j_k_ff_24_q, j_k_ff_21_q, j_k_ff_17_q);
  or or_30 (or_30_out, j_k_ff_24_q, j_k_ff_21_q, not_10_out);
  or or_31 (or_31_out, j_k_ff_24_q, not_9_out, not_10_out);
  or or_32 (or_32_out, not_8_out, j_k_ff_21_q, j_k_ff_17_q);
  or or_33 (or_33_out, not_8_out, j_k_ff_21_q, not_10_out);
  or or_34 (or_34_out, j_k_ff_24_q, j_k_ff_21_q, j_k_ff_17_q);
  or or_35 (or_35_out, j_k_ff_24_q, not_9_out, not_10_out);
  or or_36 (or_36_out, j_k_ff_24_q, j_k_ff_21_q, j_k_ff_17_q);
  or or_37 (or_37_out, j_k_ff_24_q, j_k_ff_21_q, not_10_out);
  or or_38 (or_38_out, not_8_out, j_k_ff_21_q, j_k_ff_17_q);
  or or_39 (or_39_out, not_8_out, j_k_ff_21_q, not_10_out);
  or or_40 (or_40_out, not_8_out, not_9_out, j_k_ff_17_q);
  or or_41 (or_41_out, not_8_out, not_9_out, not_10_out);
  or or_42 (or_42_out, j_k_ff_24_q, not_9_out, j_k_ff_17_q);
  or or_43 (or_43_out, not_8_out, not_9_out, j_k_ff_17_q);
  or or_44 (or_44_out, not_8_out, not_9_out, not_10_out);
  or or_45 (or_45_out, j_k_ff_24_q, j_k_ff_21_q, j_k_ff_17_q);
  or or_46 (or_46_out, not_8_out, j_k_ff_21_q, not_10_out);
  or or_47 (or_47_out, not_8_out, not_9_out, not_10_out);
  or or_48 (g_4, not_8_out, not_9_out, not_10_out);
  nand nand_3 (nand_3_out, j_k_ff_23_q, j_k_ff_18_q);
  nand nand_4 (nand_4_out, j_k_ff_18_q, j_k_ff_18_q);
  nand nand_5 (nand_5_out, j_k_ff_23_q, j_k_ff_23_q);
  nand nand_6 (nand_6_out, j_k_ff_18_q, j_k_ff_18_q);
  nand nand_7 (nand_7_out, j_k_ff_20_q, j_k_ff_20_q);
  nand nand_8 (nand_8_out, j_k_ff_23_q, j_k_ff_23_q);
  nand nand_9 (nand_9_out, j_k_ff_18_q, j_k_ff_18_q);
  nand nand_10 (g_8, j_k_ff_23_q, j_k_ff_20_q, j_k_ff_18_q);
  _7408 #(.ShowInternalStructure("true")) u_7408_5 (
    .pin1(n7408_5_pin1), .pin2(n74138_1_pin10), .pin3(n7408_5_pin3), .pin4(n7408_5_pin3),
    .pin5(n74138_1_pin9), .pin6(n7408_5_pin6), .pin13(n74138_1_pin15), .pin12(n74138_1_pin12),
    .pin11(n7408_5_pin11), .pin10(n7408_3_pin11), .pin9(n74138_1_pin11), .pin8(n7408_5_pin1));
  nand nand_11 (nand_11_out, nand_4_out, j_k_ff_20_q);
  nand nand_12 (nand_12_out, j_k_ff_23_q, j_k_ff_20_q);
  nand nand_13 (nand_13_out, nand_7_out, j_k_ff_18_q);
  nand nand_14 (nand_14_out, nand_8_out, j_k_ff_20_q);
  nand nand_15 (nand_15_out, nand_1_out, j_k_ff_18_q);
  nand nand_16 (nand_16_out, nand_2_out, j_k_ff_18_q);
  not nand_17 (nand_17_out, j_k_ff_20_q);  // NAND_Gate
  nand nand_18 (nand_18_out, nand_9_out, j_k_ff_23_q);
  nand nand_19 (nand_19_out, nand_9_out, j_k_ff_20_q);
  nand nand_20 (nand_20_out, nand_6_out, j_k_ff_20_q);
  nand nand_21 (e_8, j_k_ff_20_q, nand_15_out);
  and and_45 (c_2, or_34_out, or_35_out);
  and and_46 (e_4, or_42_out, or_43_out, or_44_out);
  and and_47 (f_4, or_45_out, or_46_out, or_47_out);
  nand nand_22 (a_8, nand_3_out, nand_3_out);
  nand nand_23 (b_8, nand_11_out, nand_12_out);
  nand nand_24 (d_8, nand_14_out, nand_14_out);
  and and_48 (d_2, or_36_out, or_37_out, or_38_out, or_39_out, or_40_out, or_41_out);
  _7408 #(.ShowInternalStructure("true")) u_7408_6 (
    .pin1(n7408_5_pin6), .pin2(n74138_1_pin7), .pin3(n7408_6_pin3));  // open: pin4, pin5, pin6, pin13, pin12, pin11, pin10, pin9, pin8
  _7408 #(.ShowInternalStructure("true")) u_7408_7 (
    .pin1(n74138_1_pin13), .pin2(n74138_1_pin7), .pin3(n7408_7_pin3), .pin4(n7408_7_pin3),
    .pin5(n74138_1_pin7), .pin6(n7408_7_pin6), .pin13(n74138_1_pin15), .pin12(n74138_1_pin10),
    .pin11(n7408_7_pin11), .pin10(n7408_7_pin11), .pin9(n74138_1_pin7), .pin8(n7408_7_pin8));
  nand nand_25 (c_8, nand_5_out, nand_20_out, nand_13_out);
  nand nand_26 (f_8, nand_16_out, nand_17_out, nand_18_out, nand_19_out);
  and and_49 (a_2, or_23_out, or_24_out, or_25_out, or_26_out, or_27_out, or_28_out);
  and and_50 (b_2, or_29_out, or_30_out, or_31_out, or_32_out, or_33_out);
  J_K_Flip_Flop j_k_ff_25 (.J(1'b1), .K(1'b1), .clk(clock_9_out), .Q(j_k_ff_25_q));  // open: Qn, preset, reset
  Clock clock_9 (.out(clock_9_out));
  J_K_Flip_Flop j_k_ff_26 (
    .J(j_k_ff_25_q), .K(j_k_ff_25_q), .clk(clock_9_out), .Q(j_k_ff_26_q));  // open: Qn, preset, reset
  J_K_Flip_Flop j_k_ff_27 (.J(1'b1), .K(1'b1), .clk(clock_10_out), .Q(j_k_ff_27_q));  // open: Qn, preset, reset
  Clock clock_10 (.out(clock_10_out));
  and and_51 (and_51_out, j_k_ff_25_q, j_k_ff_26_q);
  J_K_Flip_Flop j_k_ff_28 (
    .J(and_51_out), .K(and_51_out), .clk(clock_9_out), .Q(j_k_ff_28_q));  // open: Qn, preset, reset
  J_K_Flip_Flop j_k_ff_29 (
    .J(j_k_ff_27_q), .K(j_k_ff_27_q), .clk(clock_10_out), .Q(j_k_ff_29_q));  // open: Qn, preset, reset
  Clock clock_11 (.out(clock_11_out));
  and and_52 (and_52_out, j_k_ff_27_q, j_k_ff_29_q);
  J_K_Flip_Flop j_k_ff_30 (
    .J(and_52_out), .K(and_52_out), .clk(clock_10_out), .Q(j_k_ff_30_q));  // open: Qn, preset, reset
  J_K_Flip_Flop j_k_ff_31 (.J(1'b1), .K(1'b1), .clk(clock_11_out), .Q(j_k_ff_31_q));  // open: Qn, preset, reset
  J_K_Flip_Flop j_k_ff_32 (
    .J(j_k_ff_31_q), .K(j_k_ff_31_q), .clk(clock_11_out), .Q(j_k_ff_32_q));  // open: Qn, preset, reset
  not not_11 (not_11_out, j_k_ff_28_q);
  and and_53 (and_53_out, j_k_ff_31_q, j_k_ff_32_q);
  J_K_Flip_Flop j_k_ff_33 (
    .J(and_53_out), .K(and_53_out), .clk(clock_11_out), .Q(j_k_ff_33_q));  // open: Qn, preset, reset
  not not_12 (not_12_out, j_k_ff_26_q);
  not not_13 (not_13_out, j_k_ff_25_q);
  or or_49 (or_49_out, j_k_ff_28_q, j_k_ff_26_q);
  or or_50 (or_50_out, j_k_ff_28_q, not_12_out);
  or or_51 (or_51_out, j_k_ff_28_q, not_13_out);
  or or_52 (or_52_out, j_k_ff_28_q, j_k_ff_26_q);
  or or_53 (or_53_out, not_11_out, j_k_ff_26_q);
  or or_54 (or_54_out, j_k_ff_28_q, j_k_ff_26_q, j_k_ff_25_q);
  or or_55 (or_55_out, j_k_ff_28_q, not_13_out, not_12_out);
  or or_56 (or_56_out, j_k_ff_28_q, j_k_ff_26_q);
  or or_57 (or_57_out, not_11_out, not_12_out);
  or or_58 (or_58_out, not_11_out, j_k_ff_26_q);
  or or_59 (or_59_out, not_11_out, j_k_ff_25_q);
  or or_60 (or_60_out, not_11_out, not_12_out);
  or or_61 (or_61_out, not_11_out, not_13_out);
  or or_62 (g_6, not_11_out, not_12_out, not_13_out);
  not not_14 (not_14_out, j_k_ff_30_q);
  and and_54 (and_54_out, or_49_out, or_50_out);
  and and_55 (and_55_out, or_51_out, or_52_out);
  and and_56 (and_56_out, or_56_out, or_57_out);
  and and_57 (e_6, or_59_out, or_60_out);
  or or_63 (or_63_out, j_k_ff_28_q, j_k_ff_26_q, j_k_ff_25_q);
  not not_15 (not_15_out, j_k_ff_29_q);
  and and_58 (a_6, and_54_out, j_k_ff_25_q);
  and and_59 (f_6, or_61_out, or_63_out);
  not not_16 (not_16_out, j_k_ff_27_q);
  and and_60 (c_6, or_54_out, or_55_out);
  and and_61 (d_6, and_56_out, or_58_out);
  and and_62 (a_3, j_k_ff_30_q, j_k_ff_27_q);
  and and_63 (and_63_out, j_k_ff_29_q, not_16_out);
  and and_64 (and_64_out, j_k_ff_30_q, j_k_ff_29_q);
  xor xor_3 (xor_3_out, j_k_ff_29_q, j_k_ff_27_q);
  and and_65 (d_4, not_14_out, j_k_ff_29_q);
  and and_66 (and_66_out, not_14_out, j_k_ff_27_q);
  or or_64 (or_64_out, not_14_out, not_16_out);
  xor xor_4 (xor_4_out, j_k_ff_30_q, j_k_ff_27_q);
  or or_65 (or_65_out, not_14_out, not_15_out);
  or or_66 (c_4, xor_3_out, j_k_ff_30_q);
  or or_67 (e_3, not_15_out, and_66_out);
  and and_67 (and_67_out, or_64_out, j_k_ff_29_q);
  or or_68 (g_3, or_65_out, not_16_out);
  not not_17 (not_17_out, j_k_ff_31_q);
  not not_18 (not_18_out, j_k_ff_33_q);
  not not_19 (not_19_out, j_k_ff_32_q);
  and and_68 (b_6, and_55_out, or_53_out);
  or or_69 (b_3, and_63_out, and_64_out);
  or or_70 (f_3, and_67_out, xor_4_out);
  and and_69 (and_69_out, j_k_ff_33_q, j_k_ff_31_q);
  or or_71 (or_71_out, not_17_out, j_k_ff_33_q);
  xor xor_5 (xor_5_out, j_k_ff_32_q, j_k_ff_31_q);
  and and_70 (and_70_out, not_18_out, j_k_ff_32_q);
  and and_71 (and_71_out, not_18_out, j_k_ff_31_q);
  and and_72 (and_72_out, not_18_out, j_k_ff_32_q);
  xor xor_6 (xor_6_out, j_k_ff_33_q, j_k_ff_31_q);
  and and_73 (and_73_out, or_71_out, j_k_ff_32_q);
  or or_72 (or_72_out, xor_5_out, j_k_ff_33_q);
  or or_73 (or_73_out, and_71_out, not_19_out);
  and and_74 (and_74_out, j_k_ff_32_q, not_17_out);
  or or_74 (or_74_out, and_72_out, xor_6_out);
  or or_75 (or_75_out, not_18_out, not_19_out);
  or or_76 (or_76_out, and_74_out, or_74_out);
  or or_77 (or_77_out, not_17_out, or_75_out);
  _7_Segment_Display u_7_segment_display_3 (
    .g(or_77_out), .f(or_76_out), .a(and_69_out), .b(and_73_out), .e(or_73_out), .d(and_70_out), .c(or_72_out));  // open: dp
  // also tied to GND on the sheet: n74138_1_pin4
  // also tied to VCC on the sheet: n74138_1_pin6

  // Notes on the sheet:
  //   BASIC COMBINATIONAL CIRCUIT WITH OR-AND-XOR ICs
  //   x'
  //   y'
  //   SUM OF MINTERMS(SOM)
  //   ONLY NOR IMPLEMENTATIONS
  //   BASIC COMBINATIONAL CIRCUIT WITH OR-AND-XOR GATES
  //   Multiplexers
  //   Decoder
  //   a
  //   b
  //   c
  //   d
  //   e
  //   f
  //   g
  //   x'
  //   y'
  //   ONLY NAND IMPLEMENTATI ONS
  //   PRODUCT OF MAXTERMS
  //   w'
  //   x'
  //   y'
  //   w'
  //   x'
  //   y'
  //   STANDARD PRODUCT OF SUM
  //   STANDARD SUM OF PRODUCTS (SOP)
  //   a
  //   b
  //   c
  //   d
  //   e
  //   f
  //   g
endmodule
