// Logisim project Project_rhythm47.circ as structural Verilog: 1 circuit, main circuit main
module main (
  input  w,
  input  w_2,
  input  w_3,
  input  w_4,
  input  x,
  input  x_2,
  input  x_3,
  input  x_4,
  input  y,
  input  y_2,
  input  y_3,
  input  y_4,
  input  w_5,
  input  w_6,
  input  x_5,
  input  x_6,
  input  y_5,
  input  y_6,
  input  w_7,
  input  w_8,
  input  x_7,
  input  x_8,
  input  y_7,
  input  y_8,
  input  w_9,
  input  x_9,
  input  y_9,
  input  w_10,
  input  x_10,
  input  y_10,
  input  w_11,
  input  x_11,
  input  y_11,
  output a,
  output a_2,
  output a_3,
  output b,
  output a_4,
  output c,
  output b_2,
  output b_3,
  output d,
  output c_2,
  output c_3,
  output e,
  output d_2,
  output f,
  output b_4,
  output e_2,
  output g,
  output d_3,
  output f_2,
  output c_4,
  output e_3,
  output g_2,
  output d_4,
  output a_5,
  output f_3,
  output a_6,
  output b_5,
  output c_5,
  output d_5,
  output b_6,
  output e_4,
  output f_4,
  output g_3,
  output c_6,
  output e_5,
  output d_6,
  output g_4,
  output e_6,
  output f_5,
  output g_5,
  output f_6,
  output g_6,
  output a_7,
  output a_8,
  output b_7,
  output b_8,
  output c_7,
  output c_8,
  output d_7,
  output d_8,
  output e_7,
  output e_8,
  output f_7,
  output f_8,
  output g_7,
  output g_8
);

  wire and_3_out, and_4_out, and_6_out, and_7_out, and_8_out, and_9_out, and_10_out, and_11_out, and_12_out,
       and_13_out, and_14_out, and_15_out, and_16_out, and_17_out, and_18_out, and_19_out, and_20_out,
       and_21_out, and_22_out, and_23_out, and_24_out, and_25_out, and_26_out, and_27_out, and_28_out,
       and_29_out, and_30_out, and_31_out, and_32_out, and_33_out, and_34_out, and_35_out, and_36_out,
       and_43_out, and_44_out, and_45_out, and_46_out, and_47_out, and_48_out, and_50_out, and_51_out,
       and_53_out, and_54_out, and_55_out, and_56_out, and_57_out, multiplexer_1_out, multiplexer_2_out,
       multiplexer_3_out, multiplexer_4_out, multiplexer_5_out, multiplexer_6_out, multiplexer_7_out,
       n7404_1_pin2, n7404_1_pin4, n7404_1_pin12, n7408_1_pin3, n7408_1_pin11, n7408_3_pin1, n7408_3_pin2,
       n7408_3_pin3, n7408_3_pin5, n7408_3_pin6, n7408_3_pin9, n7408_3_pin11, n7408_3_pin12, n7408_3_pin13,
       n7408_4_pin1, n7408_4_pin3, n7408_4_pin6, n7408_4_pin11, n7408_5_pin1, n7408_5_pin3, n7408_5_pin6,
       n7408_5_pin11, n7408_6_pin3, n7408_6_pin6, n7408_6_pin8, n7408_6_pin11, n7408_7_pin3, n7432_1_pin3,
       n7432_1_pin5, n7432_1_pin8, n7432_1_pin11, n7432_1_pin12, n7432_2_pin4, n74138_1_pin4, n74138_1_pin6,
       n74138_1_pin7, n74138_1_pin9, n74138_1_pin10, nand_1_out, nand_2_out, nand_3_out, nand_4_out,
       nand_5_out, nand_6_out, nand_7_out, nand_8_out, nand_10_out, nand_11_out, nand_12_out, nand_13_out,
       nand_14_out, nand_15_out, nand_16_out, nand_17_out, nand_18_out, nand_19_out, nand_20_out, nor_1_out,
       nor_2_out, nor_3_out, nor_4_out, nor_5_out, nor_6_out, nor_7_out, nor_8_out, nor_9_out, nor_10_out,
       nor_11_out, nor_12_out, nor_13_out, nor_14_out, nor_15_out, nor_16_out, nor_17_out, nor_18_out,
       nor_19_out, nor_20_out, nor_22_out, nor_23_out, nor_24_out, nor_25_out, nor_27_out, nor_28_out,
       nor_29_out, nor_30_out, nor_31_out, nor_33_out, nor_34_out, nor_35_out, not_1_out, not_2_out,
       not_3_out, not_4_out, not_5_out, not_6_out, not_7_out, not_8_out, not_9_out, not_10_out, not_11_out,
       not_12_out, not_13_out, not_14_out, not_15_out, not_16_out, not_17_out, not_18_out, not_19_out,
       or_1_out, or_4_out, or_5_out, or_11_out, or_12_out, or_13_out, or_14_out, or_15_out, or_16_out,
       or_17_out, or_19_out, or_23_out, or_24_out, or_25_out, or_26_out, or_27_out, or_28_out, or_29_out,
       or_30_out, or_31_out, or_32_out, or_33_out, or_34_out, or_35_out, or_36_out, or_37_out, or_38_out,
       or_39_out, or_40_out, or_41_out, or_42_out, or_43_out, or_44_out, or_45_out, or_46_out, or_47_out,
       or_49_out, or_50_out, or_51_out, or_52_out, or_53_out, or_54_out, or_55_out, or_56_out, or_57_out,
       or_58_out, or_59_out, or_60_out, or_61_out, or_62_out, or_63_out, or_64_out, or_65_out, or_66_out,
       or_67_out, or_68_out, or_70_out, or_71_out, or_74_out, xor_1_out, xor_2_out, xor_3_out, xor_4_out,
       xor_5_out, xor_6_out;

  not not_1 (not_1_out, y);
  not not_2 (not_2_out, w);
  not not_3 (not_3_out, x);
  _7404 #(.ShowInternalStructure("true")) u_7404_1 (
    .pin1(y_5), .pin2(n7404_1_pin2), .pin3(x_6), .pin4(n7404_1_pin4), .pin13(w_6), .pin12(n7404_1_pin12));  // open: pin5, pin6, pin11, pin10, pin9, pin8
  and and_1 (a, w, y);
  _7408 #(.ShowInternalStructure("true")) u_7408_1 (
    .pin1(x_6), .pin2(n7404_1_pin2), .pin3(n7408_1_pin3), .pin13(n7404_1_pin12), .pin12(x_6),
    .pin11(n7408_1_pin11));  // open: pin4, pin5, pin6, pin10, pin9, pin8
  or or_1 (or_1_out, not_1_out, w);
  xor xor_1 (xor_1_out, x, y);
  _7432 #(.ShowInternalStructure("true")) u_7432_1 (
    .pin1(n7404_1_pin2), .pin2(w_6), .pin3(n7432_1_pin3), .pin4(w_6), .pin5(n7432_1_pin5), .pin6(c_5),
    .pin13(n7408_1_pin11), .pin12(n7432_1_pin12), .pin11(n7432_1_pin11), .pin10(n7404_1_pin12),
    .pin9(n7404_1_pin2), .pin8(n7432_1_pin8));
  _7432 #(.ShowInternalStructure("true")) u_7432_2 (
    .pin1(n7432_1_pin11), .pin2(n7408_1_pin3), .pin3(f_4), .pin4(n7432_2_pin4), .pin5(n7404_1_pin4),
    .pin6(e_4), .pin13(n7432_1_pin8), .pin12(n7404_1_pin4), .pin11(g_3));  // open: pin10, pin9, pin8
  and and_2 (d, not_2_out, x);
  and and_3 (and_3_out, not_2_out, y);
  and and_4 (and_4_out, not_2_out, x);
  xor xor_2 (xor_2_out, w, y);
  _7408 #(.ShowInternalStructure("true")) u_7408_2 (
    .pin1(w_6), .pin2(y_5), .pin3(a_5), .pin4(n7432_1_pin3), .pin5(x_6), .pin6(b_5), .pin13(n7404_1_pin12),
    .pin12(x_6), .pin11(d_5), .pin10(n7404_1_pin12), .pin9(y_5), .pin8(n7432_2_pin4));
  nand nand_1 (nand_1_out, y_8, y_8);
  nand nand_2 (nand_2_out, w_8, w_8);
  nand nand_3 (nand_3_out, y_8, y_8);
  nand nand_4 (nand_4_out, x_8, x_8);
  nand nand_5 (nand_5_out, w_8, w_8);
  nand nand_6 (nand_6_out, w_8, w_8);
  nand nand_7 (nand_7_out, w_8, w_8);
  nand nand_8 (nand_8_out, y_8, y_8);
  nand nand_9 (g_7, w_8, x_8, y_8);
  and and_5 (b, or_1_out, x);
  or or_2 (c, xor_1_out, w);
  or or_3 (e, and_3_out, not_3_out);
  nand nand_10 (nand_10_out, w_8, y_8);
  nand nand_11 (nand_11_out, w_8, x_8);
  nand nand_12 (nand_12_out, nand_4_out, y_8);
  nand nand_13 (nand_13_out, nand_5_out, x_8);
  nand nand_14 (nand_14_out, nand_6_out, y_8);
  nand nand_15 (nand_15_out, nand_7_out, y_8);
  not nand_16 (nand_16_out, x_8);  // NAND_Gate
  nand nand_17 (nand_17_out, nand_8_out, w_8);
  and and_6 (and_6_out, x, not_1_out);
  or or_4 (or_4_out, and_4_out, xor_2_out);
  or or_5 (or_5_out, not_2_out, not_3_out);
  _7486 #(.ShowInternalStructure("true")) u_7486_1 (
    .pin1(x_6), .pin2(y_5), .pin3(n7432_1_pin5), .pin13(w_6), .pin12(y_5), .pin11(n7432_1_pin12));  // open: pin4, pin5, pin6, pin10, pin9, pin8
  nand nand_18 (nand_18_out, nand_1_out, x_8);
  nand nand_19 (nand_19_out, nand_3_out, x_8);
  nand nand_20 (nand_20_out, nand_8_out, x_8);
  or or_6 (f, and_6_out, or_4_out);
  or or_7 (g, not_1_out, or_5_out);
  nand nand_21 (a_7, nand_10_out, nand_10_out);
  nand nand_22 (b_7, nand_18_out, nand_11_out);
  nand nand_23 (d_7, nand_13_out, nand_13_out);
  nand nand_24 (e_7, x_8, nand_14_out);
  nand nand_25 (c_7, nand_2_out, nand_19_out, nand_12_out);
  nand nand_26 (f_7, nand_15_out, nand_16_out, nand_17_out, nand_20_out);
  not not_4 (not_4_out, w_2);
  not not_5 (not_5_out, x_2);
  not not_6 (not_6_out, y_2);
  and and_7 (and_7_out, w_2, not_5_out, y_2);
  and and_8 (and_8_out, w_2, x_2, y_2);
  and and_9 (and_9_out, not_4_out, not_5_out, y_2);
  and and_10 (and_10_out, w_2, not_5_out, y_2);
  or or_8 (a_2, and_7_out, and_8_out);
  and and_11 (and_11_out, not_4_out, x_2, not_6_out);
  and and_12 (and_12_out, w_2, x_2, y_2);
  and and_13 (and_13_out, not_4_out, x_2, not_6_out);
  and and_14 (and_14_out, not_4_out, x_2, y_2);
  and and_15 (and_15_out, not_4_out, not_5_out, not_6_out);
  and and_16 (and_16_out, w_2, not_5_out, not_6_out);
  and and_17 (and_17_out, not_4_out, not_5_out, y_2);
  and and_18 (and_18_out, not_4_out, x_2, y_2);
  and and_19 (and_19_out, w_2, x_2, not_6_out);
  and and_20 (and_20_out, not_4_out, not_5_out, not_6_out);
  and and_21 (and_21_out, not_4_out, not_5_out, y_2);
  and and_22 (and_22_out, not_4_out, x_2, not_6_out);
  and and_23 (and_23_out, not_4_out, x_2, y_2);
  and and_24 (and_24_out, w_2, not_5_out, not_6_out);
  and and_25 (and_25_out, w_2, not_5_out, y_2);
  and and_26 (and_26_out, w_2, x_2, not_6_out);
  and and_27 (and_27_out, w_2, x_2, not_6_out);
  and and_28 (and_28_out, not_4_out, x_2, not_6_out);
  and and_29 (and_29_out, w_2, x_2, not_6_out);
  or or_9 (d_3, and_13_out, and_14_out);
  and and_30 (and_30_out, not_4_out, x_2, y_2);
  and and_31 (and_31_out, w_2, not_5_out, not_6_out);
  and and_32 (and_32_out, w_2, x_2, y_2);
  and and_33 (and_33_out, not_4_out, not_5_out, y_2);
  and and_34 (and_34_out, w_2, not_5_out, y_2);
  and and_35 (and_35_out, not_4_out, x_2, not_6_out);
  and and_36 (and_36_out, w_2, not_5_out, not_6_out);
  or or_10 (b_2, and_27_out, and_11_out, and_12_out);
  or or_11 (or_11_out, and_20_out, and_21_out, and_22_out);
  or or_12 (or_12_out, and_23_out, and_24_out, and_25_out);
  or or_13 (or_13_out, and_9_out, and_28_out, and_31_out);
  or or_14 (or_14_out, and_15_out, and_33_out);
  or or_15 (or_15_out, and_30_out, and_16_out, and_34_out);
  or or_16 (or_16_out, and_17_out, and_35_out, and_19_out);
  or or_17 (or_17_out, and_18_out, and_36_out);
  or or_18 (g_4, or_11_out, or_12_out, and_26_out);
  nor nor_1 (nor_1_out, w_7, w_7);
  nor nor_2 (nor_2_out, y_7, y_7);
  nor nor_3 (nor_3_out, w_7, w_7);
  nor nor_4 (nor_4_out, x_7, x_7);
  nor nor_5 (nor_5_out, w_7, w_7);
  nor nor_6 (nor_6_out, x_7, x_7);
  nor nor_7 (nor_7_out, y_7, y_7);
  nor nor_8 (nor_8_out, x_7, x_7);
  nor nor_9 (nor_9_out, x_7, x_7);
  nor nor_10 (nor_10_out, y_7, y_7);
  nor nor_11 (nor_11_out, y_7, y_7);
  nor nor_12 (nor_12_out, x_7, x_7);
  nor nor_13 (nor_13_out, w_7, w_7);
  nor nor_14 (nor_14_out, x_7, x_7);
  nor nor_15 (nor_15_out, w_7, w_7);
  nor nor_16 (nor_16_out, x_7, x_7);
  nor nor_17 (nor_17_out, y_7, y_7);
  or or_19 (or_19_out, and_29_out, and_10_out, and_32_out);
  or or_20 (f_3, or_16_out, or_17_out);
  nor nor_18 (nor_18_out, nor_3_out, nor_4_out);
  nor nor_19 (nor_19_out, nor_6_out, y_7);
  nor nor_20 (nor_20_out, nor_7_out, x_7);
  nor nor_21 (d_8, w_7, nor_8_out);
  nor nor_22 (nor_22_out, nor_10_out, w_7);
  nor nor_23 (nor_23_out, nor_12_out, w_7);
  nor nor_24 (nor_24_out, nor_13_out, y_7);
  nor nor_25 (nor_25_out, nor_14_out, y_7);
  or or_21 (c_2, or_13_out, or_19_out);
  or or_22 (e_3, or_14_out, or_15_out);
  nor nor_26 (a_8, nor_1_out, nor_2_out);
  nor nor_27 (nor_27_out, nor_4_out, y_7);
  nor nor_28 (nor_28_out, nor_5_out, nor_5_out);
  nor nor_29 (nor_29_out, w_7, nor_11_out);
  nor nor_30 (nor_30_out, nor_15_out, nor_16_out, nor_17_out);
  nor nor_31 (nor_31_out, nor_18_out, nor_27_out);
  nor nor_32 (b_8, nor_31_out, nor_31_out);
  nor nor_33 (nor_33_out, nor_28_out, nor_19_out, nor_20_out);
  nor nor_34 (nor_34_out, nor_9_out, nor_22_out);
  nor nor_35 (nor_35_out, nor_29_out, nor_23_out, nor_24_out, nor_25_out);
  nor nor_36 (g_8, nor_30_out, nor_30_out);
  nor nor_37 (c_8, nor_33_out, nor_33_out);
  nor nor_38 (e_8, nor_34_out, nor_34_out);
  nor nor_39 (f_8, nor_35_out, nor_35_out);
  not not_7 (not_7_out, w_3);
  not not_8 (not_8_out, x_3);
  not not_9 (not_9_out, y_3);
  or or_23 (or_23_out, w_3, x_3, y_3);
  or or_24 (or_24_out, w_3, x_3, not_9_out);
  or or_25 (or_25_out, w_3, not_8_out, y_3);
  or or_26 (or_26_out, w_3, not_8_out, not_9_out);
  or or_27 (or_27_out, not_7_out, x_3, y_3);
  or or_28 (or_28_out, not_7_out, not_8_out, y_3);
  or or_29 (or_29_out, w_3, x_3, y_3);
  or or_30 (or_30_out, w_3, x_3, not_9_out);
  or or_31 (or_31_out, w_3, not_8_out, not_9_out);
  or or_32 (or_32_out, not_7_out, x_3, y_3);
  or or_33 (or_33_out, not_7_out, x_3, not_9_out);
  or or_34 (or_34_out, w_3, x_3, y_3);
  or or_35 (or_35_out, w_3, not_8_out, not_9_out);
  or or_36 (or_36_out, w_3, x_3, y_3);
  or or_37 (or_37_out, w_3, x_3, not_9_out);
  or or_38 (or_38_out, not_7_out, x_3, y_3);
  or or_39 (or_39_out, not_7_out, x_3, not_9_out);
  or or_40 (or_40_out, not_7_out, not_8_out, y_3);
  or or_41 (or_41_out, not_7_out, not_8_out, not_9_out);
  or or_42 (or_42_out, w_3, not_8_out, y_3);
  or or_43 (or_43_out, not_7_out, not_8_out, y_3);
  or or_44 (or_44_out, not_7_out, not_8_out, not_9_out);
  or or_45 (or_45_out, w_3, x_3, y_3);
  or or_46 (or_46_out, not_7_out, x_3, not_9_out);
  or or_47 (or_47_out, not_7_out, not_8_out, not_9_out);
  or or_48 (g_5, not_7_out, not_8_out, not_9_out);
  _7408 #(.ShowInternalStructure("true")) u_7408_3 (
    .pin1(n7408_3_pin1), .pin2(n7408_3_pin2), .pin3(n7408_3_pin3), .pin4(n7408_3_pin3), .pin5(n7408_3_pin5),
    .pin6(n7408_3_pin6), .pin13(n7408_3_pin13), .pin12(n7408_3_pin12), .pin11(n7408_3_pin11),
    .pin10(n7408_3_pin11), .pin9(n7408_3_pin9), .pin8(n7408_3_pin1));
  _74138 #(.ShowInternalStructure("true")) u_74138_1 (
    .pin1(y_10), .pin2(x_10), .pin3(w_10), .pin4(n74138_1_pin4), .pin5(n74138_1_pin4), .pin6(n74138_1_pin6),
    .pin7(n74138_1_pin7), .pin15(n7408_3_pin13), .pin14(n7408_3_pin12), .pin13(n7408_3_pin9),
    .pin12(n7408_3_pin2), .pin11(n7408_3_pin5), .pin10(n74138_1_pin10), .pin9(n74138_1_pin9));
  and and_37 (c_4, or_34_out, or_35_out);
  _7408 #(.ShowInternalStructure("true")) u_7408_4 (
    .pin1(n7408_4_pin1), .pin2(n7408_3_pin5), .pin3(n7408_4_pin3), .pin4(n7408_4_pin3),
    .pin5(n74138_1_pin10), .pin6(n7408_4_pin6), .pin13(n7408_3_pin6), .pin12(n74138_1_pin9),
    .pin11(n7408_4_pin11), .pin10(n7408_3_pin11), .pin9(n7408_3_pin2), .pin8(n7408_4_pin1));
  _7_Segment_Display u_7_segment_display_1 (
    .g(n74138_1_pin7), .f(n7408_6_pin8), .a(n7408_4_pin11), .b(n7408_4_pin6), .e(n7408_6_pin6),
    .d(n7408_7_pin3), .c(n7408_5_pin11));  // open: dp
  and and_38 (e_5, or_42_out, or_43_out, or_44_out);
  and and_39 (f_5, or_45_out, or_46_out, or_47_out);
  and and_40 (d_4, or_36_out, or_37_out, or_38_out, or_39_out, or_40_out, or_41_out);
  and and_41 (a_4, or_23_out, or_24_out, or_25_out, or_26_out, or_27_out, or_28_out);
  and and_42 (b_4, or_29_out, or_30_out, or_31_out, or_32_out, or_33_out);
  _7408 #(.ShowInternalStructure("true")) u_7408_5 (
    .pin1(n7408_5_pin1), .pin2(n74138_1_pin10), .pin3(n7408_5_pin3), .pin4(n7408_5_pin3),
    .pin5(n74138_1_pin9), .pin6(n7408_5_pin6), .pin13(n7408_3_pin13), .pin12(n7408_3_pin2),
    .pin11(n7408_5_pin11), .pin10(n7408_3_pin11), .pin9(n7408_3_pin5), .pin8(n7408_5_pin1));
  _7408 #(.ShowInternalStructure("true")) u_7408_6 (
    .pin1(n7408_3_pin9), .pin2(n74138_1_pin7), .pin3(n7408_6_pin3), .pin4(n7408_6_pin3),
    .pin5(n74138_1_pin7), .pin6(n7408_6_pin6), .pin13(n7408_3_pin13), .pin12(n74138_1_pin10),
    .pin11(n7408_6_pin11), .pin10(n7408_6_pin11), .pin9(n74138_1_pin7), .pin8(n7408_6_pin8));
  not not_10 (not_10_out, y_9);
  not not_11 (not_11_out, w_9);
  not not_12 (not_12_out, x_9);
  _7408 #(.ShowInternalStructure("true")) u_7408_7 (
    .pin1(n7408_5_pin6), .pin2(n74138_1_pin7), .pin3(n7408_7_pin3));  // open: pin4, pin5, pin6, pin13, pin12, pin11, pin10, pin9, pin8
  Multiplexer #(.select(2)) multiplexer_1 (
    .in0(1'b0), .in1(1'b0), .in2(y_11), .in3(y_11), .out(multiplexer_1_out), .sel({w_11, x_11}));
  not not_13 (not_13_out, y_11);
  and and_43 (and_43_out, w_9, y_9);
  or or_49 (or_49_out, not_10_out, w_9);
  xor xor_3 (xor_3_out, x_9, y_9);
  Multiplexer #(.select(2)) multiplexer_2 (
    .in0(1'b0), .in1(not_13_out), .in2(1'b0), .in3(1'b1), .out(multiplexer_2_out), .sel({w_11, x_11}));
  Multiplexer #(.select(2)) multiplexer_3 (
    .in0(y_11), .in1(not_13_out), .in2(1'b1), .in3(1'b1), .out(multiplexer_3_out), .sel({w_11, x_11}));
  Multiplexer #(.select(2)) multiplexer_4 (
    .in0(1'b0), .in1(1'b1), .in2(1'b0), .in3(1'b0), .out(multiplexer_4_out), .sel({w_11, x_11}));
  Multiplexer #(.select(2)) multiplexer_5 (
    .in0(1'b1), .in1(y_11), .in2(1'b1), .in3(1'b0), .out(multiplexer_5_out), .sel({w_11, x_11}));
  Multiplexer #(.select(2)) multiplexer_6 (
    .in0(y_11), .in1(1'b1), .in2(not_13_out), .in3(not_13_out), .out(multiplexer_6_out), .sel({w_11, x_11}));
  Multiplexer #(.select(2)) multiplexer_7 (
    .in0(1'b1), .in1(1'b1), .in2(1'b1), .in3(not_13_out), .out(multiplexer_7_out), .sel({w_11, x_11}));
  and and_44 (and_44_out, not_11_out, x_9);
  and and_45 (and_45_out, not_11_out, y_9);
  and and_46 (and_46_out, not_11_out, x_9);
  xor xor_4 (xor_4_out, w_9, y_9);
  not not_14 (not_14_out, w_4);
  not not_15 (not_15_out, x_4);
  not not_16 (not_16_out, w_5);
  not not_17 (not_17_out, x_5);
  and and_47 (and_47_out, or_49_out, x_9);
  or or_50 (or_50_out, xor_3_out, w_9);
  or or_51 (or_51_out, and_45_out, not_12_out);
  or or_52 (or_52_out, and_46_out, xor_4_out);
  not not_18 (not_18_out, y_4);
  not not_19 (not_19_out, y_6);
  and and_48 (and_48_out, x_9, not_10_out);
  or or_53 (or_53_out, not_11_out, not_12_out);
  _7_Segment_Display u_7_segment_display_2 (
    .g(multiplexer_7_out), .f(multiplexer_6_out), .a(multiplexer_1_out), .b(multiplexer_2_out),
    .e(multiplexer_5_out), .d(multiplexer_4_out), .c(multiplexer_3_out));  // open: dp
  and and_49 (a_3, w_4, y_4);
  and and_50 (and_50_out, x_4, not_18_out);
  and and_51 (and_51_out, w_4, x_4);
  xor xor_5 (xor_5_out, x_4, y_4);
  and and_52 (d_2, not_14_out, x_4);
  and and_53 (and_53_out, not_14_out, y_4);
  or or_54 (or_54_out, not_14_out, not_18_out);
  xor xor_6 (xor_6_out, w_4, y_4);
  or or_55 (or_55_out, not_14_out, not_15_out);
  or or_56 (or_56_out, w_5, x_5);
  or or_57 (or_57_out, w_5, not_17_out);
  or or_58 (or_58_out, w_5, not_19_out);
  or or_59 (or_59_out, w_5, x_5);
  or or_60 (or_60_out, not_16_out, x_5);
  or or_61 (or_61_out, w_5, x_5, y_6);
  or or_62 (or_62_out, w_5, not_19_out, not_17_out);
  or or_63 (or_63_out, w_5, x_5);
  or or_64 (or_64_out, not_16_out, not_17_out);
  or or_65 (or_65_out, not_16_out, x_5);
  or or_66 (or_66_out, not_16_out, y_6);
  or or_67 (or_67_out, not_16_out, not_17_out);
  or or_68 (or_68_out, not_16_out, not_19_out);
  or or_69 (g_6, not_16_out, not_17_out, not_19_out);
  or or_70 (or_70_out, and_48_out, or_52_out);
  or or_71 (or_71_out, not_10_out, or_53_out);
  or or_72 (e_2, not_15_out, and_53_out);
  and and_54 (and_54_out, or_54_out, x_4);
  or or_73 (g_2, or_55_out, not_18_out);
  and and_55 (and_55_out, or_56_out, or_57_out);
  and and_56 (and_56_out, or_58_out, or_59_out);
  and and_57 (and_57_out, or_63_out, or_64_out);
  and and_58 (e_6, or_66_out, or_67_out);
  or or_74 (or_74_out, w_5, x_5, y_6);
  or or_75 (b_3, and_50_out, and_51_out);
  or or_76 (c_3, xor_5_out, w_4);
  or or_77 (f_2, and_54_out, xor_6_out);
  and and_59 (a_6, and_55_out, y_6);
  and and_60 (f_6, or_68_out, or_74_out);
  and and_61 (c_6, or_61_out, or_62_out);
  and and_62 (d_6, and_57_out, or_65_out);
  _7_Segment_Display u_7_segment_display_3 (
    .g(or_71_out), .f(or_70_out), .a(and_43_out), .b(and_47_out), .e(or_51_out), .d(and_44_out), .c(or_50_out));  // open: dp
  and and_63 (b_6, and_56_out, or_60_out);
  // also tied to GND on the sheet: n74138_1_pin4
  // also tied to VCC on the sheet: n74138_1_pin6

  // Notes on the sheet:
  //   BASIC COMBINATIONAL CIRCUIT WITH OR-AND-XOR GATES
  //   BASIC COMBINATIONAL CIRCUIT WITH OR-AND-XOR ICs
  //   ONLY NAND IMPLEMENTATI ONS
  //   w'
  //   x'
  //   y'
  //   SUM OF MINTERMS(SOM)
  //   ONLY NOR IMPLEMENTATIONS
  //   w'
  //   x'
  //   y'
  //   PRODUCT OF MAXTERMS
  //   a
  //   b
  //   c
  //   d
  //   w'
  //   w'
  //   e
  //   f
  //   g
  //   x'
  //   x'
  //   SEVEN SEGMENT DISPLAY
  //   y'
  //   y'
  //   STANDARD SUM OF PRODUCTS (SOP)
  //   STANDARD PRODUCT OF SUM
  //   a
  //   b
  //   c
  //   d
  //   e
  //   f
  //   g
endmodule
